# Fritzing sketch Automation Sketch (saved by Fritzing 0.9.3b)
breadboards: 1

parts:
  8_Channel_Relay1 = 8 Channel Power Relay
  F1 = Fan - Ventilador [package=THT]
  F2 = Fan - Ventilador [package=THT]
  U1 = ESP32S-HiLetgo [part_number=ESP32S-HiLetgo]
  F3 = Fan - Ventilador [package=THT]  # not connected
  F4 = Fan - Ventilador [package=THT]
  BULB1 = LEDs [package=led10mm]  # not connected
  BULB4 = LEDs [package=led10mm]  # not connected
  BULB2 = LEDs [package=led10mm]  # not connected
  BULB3 = LEDs [package=led10mm]  # not connected

nets:
  GND: 8_Channel_Relay1.GND, F1.GND, F2.GND, U1.GND, F4.GND
  N1: 8_Channel_Relay1.IN1, U1.GPIO25
  N2: 8_Channel_Relay1.IN2, U1.GPIO26
  N3: 8_Channel_Relay1.IN3, U1.GPIO32
  N4: 8_Channel_Relay1.IN4, U1.GPIO33
  N5: 8_Channel_Relay1.IN5, U1.GPIO27
  N6: 8_Channel_Relay1.IN6, U1.GPIO14
  N7: 8_Channel_Relay1.IN7, U1.GPIO13
  N8: 8_Channel_Relay1.IN8, U1.GPIO16
  VCC: 8_Channel_Relay1.VCC, U1.VIN
  N9: 8_Channel_Relay1.COM, U1.3.3
  N10: 8_Channel_Relay1.NO#23, F1.5V
  N11: 8_Channel_Relay1.NO#38, F4.5V
  N12: 8_Channel_Relay1.NO#44, F2.5V

custom parts:
  8 Channel Power Relay: An 8 channel power relay. The module operates at 5V.
  Fan - Ventilador: Ventilador de 2 pines, se encuentra comunmente en computadoras de escritorio
  ESP32S-HiLetgo: HiLetgo ESP-WROOM-32 ESP32 ESP-32S Development Board 2.4GHz Dual-Mode WiFi + Bluetooth Dual Cores Microcontroller The ESP32 integrated with Antenna switches, RF Balun, power amplifiers, low-noise amplifiers, filters, and management modules, and the entire solution occupies the least area of PCB. 2.4 GHz Wi-Fi plus Bluetooth dual-mode chip, with TSMC Ultra-low power consumption 40nm technology,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
